# Fritzing sketch sketch (saved by Fritzing 0.8.3b)
breadboards: 1

parts:
  Part1 = Arduino Uno (Rev3)
  R1 = Resistor [tolerance=±5% resistance=100k package=THT]
  R2 = Resistor [tolerance=±5% resistance=100k package=THT]
  R3 = Resistor [tolerance=±5% resistance=100k package=THT]

nets:
  N1: Part1.D8, R1.Pin_1
  N2: Part1.D2, R3.Pin_1
  N3: Part1.D4, R1.Pin_0, R2.Pin_0, R3.Pin_0
  N4: Part1.D6_PWM, R2.Pin_1
