# Fritzing sketch sketch (saved by Fritzing 0.8.3b)

parts:
  Part1 = Arduino Uno (Rev3)
  Part2 = IR Receiver Breakout [package=PCB]

nets:
  N1: Part1.ICSP_MOSI, Part1.D11_PWM/MOSI, Part2.VCC
  GND: Part1.GND, Part2.GND
  N2: Part1.5V, Part2.OUT
