# Fritzing sketch sketch (saved by Fritzing 0.8.3b)
breadboards: 1

parts:
  R1 = Resistor [tolerance=±5% resistance=220 package=THT]
  R2 = Resistor [tolerance=±5% resistance=220 package=THT]
  S1 = Momentary Switch [package=ksa_sealed_tac_switch]
  S2 = Momentary Switch [package=ksa_sealed_tac_switch]
  Part1 = Arduino Uno (Rev3)
  LED1 = LED - 5mm [color="Yellow (592nm)" package="5 mm [THT]"]
  LED2 = LED - 5mm [color="Green (555nm)" package="5 mm [THT]"]

nets:
  N1: R1.Pin_0, S1.2
  N2: R1.Pin_1, R2.Pin_1, Part1.GND, LED1.cathode, LED2.cathode
  N3: R2.Pin_0, S2.2
  N4: S1.1, Part1.D9_PWM
  N5: S1.4, S2.4, Part1.5V
  N6: S2.1, Part1.D7
  N7: Part1.D8, LED1.anode
  N8: Part1.D6_PWM, LED2.anode
