# Fritzing sketch plan (saved by Fritzing 0.7.12b)
breadboards: 1

parts:
  Arduino1 = Arduino
  R1 = Rotary Potentiometer (Small) [maximum_resistance=100kΩ]
  RE1 = Rotary Encoder [package=THT]
  Part1 = Ambient Light Sensor (TEMT6000 Breakout Board)

nets:
  +5V: Arduino1.+5V, R1.leg1, RE1.EncoderPinB, Part1.VCC
  GND: Arduino1.GND, R1.leg2, RE1.EncoderPinC, Part1.GND
  N1: Arduino1.A0, R1.wiper
  N2: Arduino1.A1, RE1.EncoderPinA
  N3: Arduino1.A2, Part1.S
